# Fritzing sketch MultiLedSequence (saved by Fritzing 0.9.1b)
breadboards: 1

parts:
  Part1 = Arduino Uno (Rev3)
  LED1 = smd LED [color="Red (633nm)" package="0805 [SMD]"]
  R1 = Resistor [tolerance=±5% resistance=220 package="1206 [SMD]"]
  R2 = Resistor [tolerance=±5% resistance=220 package="1206 [SMD]"]
  LED2 = smd LED [color="Red (633nm)" package="0805 [SMD]"]
  LED3 = smd LED [color="Red (633nm)" package="0805 [SMD]"]
  LED5 = smd LED [color="Red (633nm)" package="0805 [SMD]"]
  R3 = Resistor [tolerance=±5% resistance=220 package="1206 [SMD]"]
  R4 = Resistor [tolerance=±5% resistance=220 package="1206 [SMD]"]
  R5 = Resistor [tolerance=±5% resistance=220 package="1206 [SMD]"]
  LED4 = smd LED [color="Red (633nm)" package="0805 [SMD]"]

nets:
  N1: Part1.D9_PWM, R3.Pin_0
  N2: Part1.D10_PWM/SS, R2.Pin_0
  N3: Part1.D11_PWM/MOSI, R1.Pin_0
  N4: Part1.GND, LED1.cathode, LED2.cathode, LED3.cathode, LED5.cathode, LED4.cathode
  N5: Part1.D5_PWM, R5.Pin_0
  N6: Part1.D6_PWM, R4.Pin_0
  N7: LED1.anode, R1.Pin_1
  N8: R2.Pin_1, LED2.anode
  N9: LED3.anode, R3.Pin_1
  N10: LED5.anode, R5.Pin_1
  N11: R4.Pin_1, LED4.anode

// code stored in the sketch: Led blink.ino
int pinLed = 13;


void setup() {                
  pinMode(led, OUTPUT);     
}


void loop() {
  digitalWrite(pinLed, HIGH);   // turn the LED on (HIGH is the voltage level)
  delay(1000);                  // wait for a second
  digitalWrite(pinLed, LOW);    // turn the LED off by making the voltage LOW
  delay(1000);                  // wait for a second
}
