# Fritzing sketch RgbStripSerial (saved by Fritzing 0.9.3b)

parts:
  Part1 = Arduino Uno (Rev3)
  WS2812_Compatible_Led_Strip = Neopixel Strip -- Black (30/m)
  5V_DC = Power plug

nets:
  N1: Part1.D6_PWM, WS2812_Compatible_Led_Strip.Din
  GND: Part1.GND, WS2812_Compatible_Led_Strip.GND, 5V_DC.GND
  VIN: Part1.VIN, WS2812_Compatible_Led_Strip.+5V, 5V_DC.VCC

custom parts:
  Neopixel Strip -- Black (30/m): These NeoPixel strips have 30 digitally-addressable pixel LEDs per meter and are very affordable and are only 12.5 mm wide, 10 mm if you remove the strip from the casing.

// code stored in the sketch: Led blink.ino
int pinLed = 13;


void setup() {                
  pinMode(led, OUTPUT);     
}


void loop() {
  digitalWrite(pinLed, HIGH);   // turn the LED on (HIGH is the voltage level)
  delay(1000);                  // wait for a second
  digitalWrite(pinLed, LOW);    // turn the LED off by making the voltage LOW
  delay(1000);                  // wait for a second
}
