# Fritzing sketch SimpleLed (saved by Fritzing 0.9.1b)
breadboards: 1

parts:
  Part1 = Arduino Uno (Rev3)
  LED1 = smd LED [color="Red (633nm)" package="0805 [SMD]"]
  R1 = Resistor [tolerance=±5% resistance=220 package="1206 [SMD]"]

nets:
  N1: Part1.D11_PWM/MOSI, R1.Pin_0
  N2: Part1.GND, LED1.cathode
  N3: LED1.anode, R1.Pin_1

// code stored in the sketch: Led blink.ino
int pinLed = 13;


void setup() {                
  pinMode(led, OUTPUT);     
}


void loop() {
  digitalWrite(pinLed, HIGH);   // turn the LED on (HIGH is the voltage level)
  delay(1000);                  // wait for a second
  digitalWrite(pinLed, LOW);    // turn the LED off by making the voltage LOW
  delay(1000);                  // wait for a second
}
