# Fritzing sketch SimpleTlc5940 (saved by Fritzing 0.9.1b)
breadboards: 1

parts:
  Part1 = Arduino Uno (Rev3)
  U1 = Packages: [package=dil28-3]
  R1 = Resistor [tolerance=±5% resistance=10k package="1206 [SMD]"]
  R2 = Resistor [tolerance=±5% resistance=2.2k package="1206 [SMD]"]
  D1 = LED_BARGRAPH_10 [package=led_bargaph_10]

nets:
  N1: Part1.D9_PWM, U1.XLAT
  N2: Part1.D10_PWM/SS, U1.BLANK, R1.Pin_1
  N3: Part1.D11_PWM/MOSI, U1.SIN
  N4: Part1.D13/SCK, U1.SCLK
  5V: Part1.5V, U1.DCPRG, U1.VCC, R1.Pin_0, D1.A_A, D1.B_A, D1.C_A, D1.D_A, D1.E_A, D1.F_A, D1.G_A, D1.H_A, D1.I_A, D1.J_A
  GND: Part1.GND, U1.GND, U1.VPRG, R2.Pin_0
  N5: U1.OUT1, D1.A_C
  N6: U1.OUT2, D1.B_C
  N7: U1.OUT3, D1.C_C
  N8: U1.OUT4, D1.D_C
  N9: U1.OUT5, D1.E_C
  N10: U1.OUT6, D1.F_C
  N11: U1.OUT7, D1.G_C
  N12: U1.OUT8, D1.H_C
  N13: U1.OUT9, D1.I_C
  N14: U1.OUT10, D1.J_C
  N15: U1.IREF, R2.Pin_1

// code stored in the sketch: Led blink.ino
int pinLed = 13;


void setup() {                
  pinMode(led, OUTPUT);     
}


void loop() {
  digitalWrite(pinLed, HIGH);   // turn the LED on (HIGH is the voltage level)
  delay(1000);                  // wait for a second
  digitalWrite(pinLed, LOW);    // turn the LED off by making the voltage LOW
  delay(1000);                  // wait for a second
}
